# Fritzing sketch Still-Monitor-and-Controller (saved by Fritzing 0.9.9b)
breadboards: 4

parts:
  HLK-PM1 = HLK-PM12 [part_number=HLK-PM12]
  IC1 = Voltage Regulator LM1117 [package=sot223]
  Raspberry_Pi_1 = Raspberry Pi 3 [part_number=RPI-3-V1.2]
  U1 = DC-DC_CONVERTER [package=dc-dc_converter]
  J1 = Camdenboss CTB0158-3 [part_number=CTB0158-3 package=THT]
  J2 = Camdenboss CTB0158-3 [part_number=CTB0158-3 package=THT]
  J3 = Camdenboss CTB0158-2 [part_number=CTB0158-2 package=THT]
  J4 = Camdenboss CTB0158-3 [part_number=CTB0158-3 package=THT]
  J5 = Camdenboss CTB0158-3 [part_number=CTB0158-3 package=THT]
  J6 = Camdenboss CTB0158-2 [part_number=CTB0158-2 package=THT]
  J7 = Camdenboss CTB0158-2 [part_number=CTB0158-2 package=THT]
  J8 = Camdenboss CTB0158-2 [part_number=CTB0158-2 package=THT]
  J9 = Camdenboss CTB0158-2 [part_number=CTB0158-2 package=THT]
  R2 = Resistor [tolerance=±5% power=0.25 resistance=10k package=THT]
  R5 = Resistor [tolerance=±5% power=0.25 resistance=10k package=THT]
  R6 = Resistor [tolerance=±5% power=0.25 resistance=10k package=THT]
  R7 = Resistor [tolerance=±5% power=0.25 resistance=10k package=THT]
  U2 = L298_BRIDGE_DRIVER [package=powerso20]
  J10 = Camdenboss CTB0158-2 [part_number=CTB0158-2 package=THT]
  J11 = Camdenboss CTB0158-2 [part_number=CTB0158-2 package=THT]
  Part1 = I2C level shifter bidirectional
  Part2 = I2C level shifter bidirectional
  R8 = Resistor [tolerance=±5% power=0.25 resistance=220 package=THT]
  R9 = Resistor [tolerance=±5% power=0.25 resistance=220 package=THT]
  R10 = Resistor [tolerance=±5% power=0.25 resistance=220 package=THT]
  R11 = Resistor [tolerance=±5% power=0.25 resistance=220 package=THT]
  LED1 = smd LED [color="Red (633nm)" package="0805 [SMD]"]
  LED2 = smd LED [color="Green (560nm)" package="0805 [SMD]"]
  LED3 = smd LED [color="Red (633nm)" package="0805 [SMD]"]
  LED4 = smd LED [color="Green (565nm)" package="0805 [SMD]"]
  M1 = DC Motor
  M2 = DC Motor
  J12 = Camdenboss CTB0158-3 [part_number=CTB0158-3 package=THT]
  J13 = Camdenboss CTB0158-3 [part_number=CTB0158-3 package=THT]
  J14 = Camdenboss CTB0158-2 [part_number=CTB0158-2 package=THT]
  J15 = Camdenboss CTB0158-2 [part_number=CTB0158-2 package=THT]
  DRV_1 = DRV 8825 Stepper Motor Carrier, High Current [part_number="DRV 8825"]
  C1 = Capacitor Polarized [package=cpol-radial-100uf-25v]
  M4 = Stepper Motor - Bipolar
  S1 = SPST Switch [package=r_sw_th]
  S2 = SPST Switch [package=r_sw_th]
  J16 = Camdenboss CTB0158-3 [part_number=CTB0158-3 package=THT]
  J17 = Camdenboss CTB0158-3 [part_number=CTB0158-3 package=THT]
  J18 = Camdenboss CTB0158-3 [part_number=CTB0158-3 package=THT]
  RHT1 = Humidity and Temperature Sensor RHT03
  RHT2 = Humidity and Temperature Sensor RHT03
  RHT3 = Humidity and Temperature Sensor RHT03
  R12 = Resistor [tolerance=±5% resistance=4.7k package="0603 [SMD]"]

nets:
  N1: HLK-PM1.-Vo, U1.GND1
  VIN: HLK-PM1.+Vo, U1.VIN, U2.VSS, J13.pin3, C1.+
  VCC: IC1.OUT, Raspberry_Pi_1.5V, J1.pin1, J1.pin2, J1.pin3, J2.pin1, J2.pin2, J2.pin3, J8.pin1, J9.pin1, J9.pin2, R2.Pin_1, R5.Pin_1, R6.Pin_1, R7.Pin_1, U2.VS, Part2.HV, J13.pin1, J16.pin3, J17.pin3, J18.pin3, RHT1.Vcc, RHT2.Vcc, RHT3.Vcc, R12.Pin_1
  N2: IC1.IN, U1.VOUT
  N3: Raspberry_Pi_1.GIPO4, J16.pin2, J17.pin2, J18.pin2, RHT1.Data-signal, RHT2.Data-signal, RHT3.Data-signal, R12.Pin_0
  N4: Raspberry_Pi_1.GIPO22, J6.pin1, R6.Pin_0, S2.P
  N5: Raspberry_Pi_1.GIPO11, J12.pin1
  N6: Raspberry_Pi_1.GIPO13, J12.pin3
  N7: Raspberry_Pi_1.GIPO19, J7.pin2, R5.Pin_0
  N8: Raspberry_Pi_1.GIPO21, J11.pin1, Part1.LV4, R10.Pin_0
  N9: Raspberry_Pi_1.GIPO20, J11.pin2, Part1.LV1, R11.Pin_0
  N10: Raspberry_Pi_1.GIPO12, J12.pin2
  GND: Raspberry_Pi_1.GND, U1.GND2, J3.pin1, J3.pin2, J4.pin1, J4.pin2, J4.pin3, J5.pin1, J5.pin2, J5.pin3, U2.GND, Part2.GND, LED1.anode, LED2.anode, LED3.anode, LED4.anode, J13.pin2, DRV_1.GROUND_LOG, C1.-, J16.pin1, J17.pin1, J18.pin1, RHT1.GND_2, RHT2.GND_2, RHT3.GND_2
  N11: Raspberry_Pi_1.GIPO25, J10.pin1, Part2.LV3, R8.Pin_0
  N12: Raspberry_Pi_1.GIPO24, J10.pin2, Part2.LV2, R9.Pin_0
  N13: Raspberry_Pi_1.GIPO23, J6.pin2, R7.Pin_0
  N14: Raspberry_Pi_1.GIPO18, J7.pin1, R2.Pin_0, S1.P
  N15: U2.OUT1, M2.pin_2
  N16: U2.OUT2, M2.pin_1
  N17: U2.IN1, Part1.HV1
  N18: U2.IN2, Part1.HV3
  N19: U2.IN3, Part2.HV2
  N20: U2.IN4, Part2.HV3
  N21: U2.OUT3, M1.pin_2
  N22: U2.OUT4, M1.pin_1
  N23: R8.Pin_1, LED1.cathode
  N24: R9.Pin_1, LED2.cathode
  N25: R10.Pin_1, LED3.cathode
  N26: R11.Pin_1, LED4.cathode
  N27: J14.pin1, M4.D
  N28: J15.pin1, DRV_1.OUT_1B, M4.C
  N29: J15.pin2, M4.A

notes:
  POWER BREAK OUT BOARD
  VALVE CONTROL BOARD
  HEATING STEPPER CONTROL BOARD
  INTERFACE BOARD
